# Fritzing sketch RelayModule (saved by Fritzing 0.9.3b)
circuit board: 10.9891cm x 6.55898cm
breadboards: 2

parts:
  R1 = Resistor [tolerance=±5% resistance=150 package=THT]
  LED1 = LED - 5mm [color="Red (633nm)" package="5 mm [THT]"]
  J1 = shrouded pin header, 10 pins [form="♂ (shrouded male)"]
  J2 = screw terminal, 9 pins
  U1 = RELAY [package=relay-jzc]
  U2 = RELAY [package=relay-jzc]
  U3 = RELAY [package=relay-jzc]
  U4 = RELAY [package=relay-jzc]
  U5 = RELAY [package=relay-jzc]
  U6 = RELAY [package=relay-jzc]
  U7 = RELAY [package=relay-jzc]
  U8 = RELAY [package=relay-jzc]

nets:
  N1: R1.Pin_0, J1.pin10, U1.COIL2, U2.COIL2, U3.COIL2, U4.COIL2, U5.COIL2, U6.COIL2, U7.COIL2, U8.COIL2
  N2: R1.Pin_1, LED1.cathode
  N3: LED1.anode, J1.pin1
  N4: J1.pin2, U1.COIL1
  N5: J1.pin3, U2.COIL1
  N6: J1.pin4, U3.COIL1
  N7: J1.pin5, U4.COIL1
  N8: J1.pin6, U5.COIL1
  N9: J1.pin7, U8.COIL1
  N10: J1.pin8, U7.COIL1
  N11: J1.pin9, U6.COIL1
  N12: J2.pin1, U1.NO
  N13: J2.pin2, U2.NO
  N14: J2.pin3, U3.NO
  N15: J2.pin4, U4.NO
  N16: J2.pin5, U5.NO
  N17: J2.pin6, U6.NO
  N18: J2.pin7, U7.NO
  N19: J2.pin8, U8.NO
  N20: J2.pin9, U1.MAIN, U2.MAIN, U3.MAIN, U4.MAIN, U5.MAIN, U6.MAIN, U7.MAIN, U8.MAIN

notes:
  1
  2
  COM
  3
  4
  6
  5
  7
  8
  PWR
  FAB 00100 ASSY 00101
  CLCRM, CLController Relay Module.     Designer: Cyrus Brunner, 1.0
  +5V DC
  REL 1
  REL 2
  OUT 1
  OUT 2
  OUT 3
  OUT 4
  OUT 5
  OUT 6
  OUT 7
  OUT 8
  REL 3
  REL 4
  REL 5
  REL 8
  REL 7
  REL 6
  CLCRM Rev 1.0
  Copyright (c) 2020 Cyrus Brunner
  www.cyrusbuilt.net
  CLController Relay Module
